// Logisim project Demultiplexer.circ as structural Verilog: 1 circuit, main circuit main
module main (
  input  A,
  input  B,
  input  data_A
);

  wire and_1_out, and_2_out, and_3_out, and_4_out, not_1_out, not_2_out;

  not not_1 (not_1_out, A);
  not not_2 (not_2_out, B);
  and and_1 (and_1_out, data_A, not_1_out, not_1_out, not_2_out);
  and and_2 (and_2_out, data_A, not_1_out, not_1_out, B);
  and and_3 (and_3_out, data_A, A, A, not_2_out);
  and and_4 (and_4_out, data_A, A, B);
  LED led_1 (.in(and_1_out));
  LED led_2 (.in(and_2_out));
  LED led_3 (.in(and_3_out));
  LED led_4 (.in(and_4_out));

  // Notes on the sheet:
  //   Demultiplexer
  //   IO
  //   I1
  //   I2
  //   I3
endmodule
