// Logisim project Encoder.circ as structural Verilog: 1 circuit, main circuit main
module main (
  input  D7,
  input  D6,
  input  D5,
  input  in_4,
  input  D3,
  input  D2,
  input  D1,
  input  D0
);

  wire or_1_out, or_2_out, or_3_out;

  or or_1 (or_1_out, in_4, D7, D6, D5);
  or or_2 (or_2_out, D2, D7, D3, D6);
  or or_3 (or_3_out, D1, D3, D5, D7);
  LED led_1 (.in(or_1_out));
  LED led_2 (.in(or_2_out));
  LED led_3 (.in(or_3_out));

  // Notes on the sheet:
  //   ENCODER
  //   D4
  //   A
  //   B
  //   C
endmodule
