// Logisim project Half-Adder.circ as structural Verilog: 1 circuit, main circuit main
module main (
  input  A,
  input  B
);

  wire and_1_out, and_2_out, and_3_out, not_1_out, not_2_out, or_1_out;

  not not_1 (not_1_out, B);
  not not_2 (not_2_out, A);
  and and_1 (and_1_out, A, not_1_out, not_1_out);
  and and_2 (and_2_out, B, not_2_out, not_2_out, not_2_out);
  and and_3 (and_3_out, B, A);
  LED led_1 (.in(and_3_out));
  or or_1 (or_1_out, and_1_out, and_1_out, and_2_out);
  LED led_2 (.in(or_1_out));

  // Notes on the sheet:
  //   Half Adder
  //   Carry
  //   Out Put
endmodule
