// Logisim project Logical-Gates.circ as structural Verilog: 1 circuit, main circuit main
module main (
  input  A,
  input  B,
  input  A_2,
  input  B_2,
  input  A_3,
  input  B_3,
  input  A_4,
  input  B_4,
  input  A_5,
  input  A_6,
  input  B_5
);

  wire and_1_out, and_2_out, and_3_out, and_4_out, nor_1_out, not_1_out, not_2_out, not_3_out, not_4_out,
       not_5_out, or_1_out, or_2_out;

  not not_1 (not_1_out, A_6);
  not not_2 (not_2_out, B_5);
  nor nor_1 (nor_1_out, A, B);
  and and_1 (and_1_out, A_2, A_2, B_2);
  and and_2 (and_2_out, A_3, B_3);
  or or_1 (or_1_out, A_4, B_4);
  not not_3 (not_3_out, A_5);
  and and_3 (and_3_out, not_2_out, not_1_out);
  and and_4 (and_4_out, not_2_out, not_1_out);
  LED led_1 (.in(not_4_out));
  not not_4 (not_4_out, nor_1_out);
  not not_5 (not_5_out, and_1_out);
  LED led_2 (.in(not_5_out));
  LED led_3 (.in(and_2_out));
  LED led_4 (.in(or_1_out));
  LED led_5 (.in(not_3_out));
  or or_2 (or_2_out, and_3_out, and_4_out, and_4_out);
  LED led_6 (.in(or_2_out));

  // Notes on the sheet:
  //   NAND
  //   AND
  //   OR
  //   XOR
  //   NOR
  //   NOT
  //   Out Put
  //   Out Put
  //   Out Put
  //   Out Put
  //   Out Put
  //   Out Put
endmodule
