// Logisim project Subtractor.circ as structural Verilog: 1 circuit, main circuit main
module main (
  input  A,
  input  B,
  input  in_3
);

  wire and_1_out, and_2_out, not_1_out, not_2_out, or_1_out, xor_1_out, xor_2_out;

  not not_1 (not_1_out, A);
  xor xor_1 (xor_1_out, A, B);
  and and_1 (and_1_out, B, not_1_out);
  xor xor_2 (xor_2_out, xor_1_out, in_3);
  not not_2 (not_2_out, xor_1_out);
  LED led_1 (.in(xor_2_out));
  and and_2 (and_2_out, in_3, not_2_out, not_2_out);
  or or_1 (or_1_out, and_2_out, and_1_out, and_1_out);
  LED led_2 (.in(or_1_out));

  // Notes on the sheet:
  //   Borrow In
  //   Full Subtractor
  //   Difference
  //    B Out Put
endmodule
